# Fritzing sketch Morse Clock Sketch (saved by Fritzing 0.9.9b)
breadboards: 1

parts:
  IC2 = PICAXE-18M [package=THT]
  J1 = Piezo Speaker
  S2 = Tilt Switch [package=THT]
  R1 = Resistor [tolerance=±5% resistance=150 package="1206 [SMD]"]  # not connected
  R3 = Resistor [tolerance=±5% resistance=150 package="0402 [SMD]"]  # not connected
  R4 = Resistor [tolerance=±5% resistance=10k package="2512 [SMD]"]
  R5 = Resistor [tolerance=±5% resistance=100 package="2010 [SMD]"]  # not connected
  R6 = Resistor [tolerance=±5% resistance=150 package="0805 [SMD]"]
  M1 = TP4056 Module [part_number=HW-107]
  Part3 = Adafruit DS1307 RTC Breakout [part_number="Adafruit #264"]
  LED1 = RGB LED (com. anode, rbg) [package="5 mm [THT]"]
  Bat1 = battery_holder_single_18650  # not connected

nets:
  N1: IC2.0V, R4.Pin_1, M1.pin2, Part3.GND
  N2: IC2.Out_1, Part3.SDA
  N3: IC2.Out_3, S2.Pin_2
  N4: IC2.Out_4, Part3.SCL, LED1.common_anode
  N5: IC2.+V, S2.Pin_1, R4.Pin_0, M1.pin5, Part3.VCC
  N6: IC2.In_7_/_Keyboard_Data, R6.Pin_1
  N7: J1.pin1, LED1.blue_cathode

custom parts:
  TP4056 Module: TP4056 Lithium Battery Charge Management Module Links: TP4056 website
  Adafruit DS1307 RTC Breakout: This is a great battery-backed real time clock (RTC) that allows your microcontroller project to keep track of time even if it is reprogrammed, or if the power is lost. Perfect for datalogging, clock-building, time stamping, timers and alarms, etc. The DS1307 is the most popular RTC - but it requires 5V power to work (although we've used it with 5V power and 3.3V logic successfully) PCB &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
  battery_holder_single_18650: single 18650 battery holder
